# Fritzing sketch boxduino (saved by Fritzing 0.9.2b)
breadboards: 1

parts:
  Part1 = Arduino Nano (Rev3.0) (ICSP)
  R2 = Resistor [tolerance=±5% resistance=100k package=THT]
  S1 = Pushbutton [package="[THT]"]
  R3 = Resistor [tolerance=±5% resistance=1k package=THT]
  Q1 = MOSFET-NCHANNEL [part_number=3034 package=to220v]
  Connector_+_GND = female pin header, 2 pins [form="♀ (female)"]
  R4 = Resistor [tolerance=±5% resistance=1k package=THT]
  R6 = Rotary Potentiometer (Small) [maximum_resistance=50k package=THT]
  R5 = Resistor [tolerance=±5% resistance=1M package=THT]
  J1 = male alternating pin header, 8 pins [form="♂ (male)"]
  U2 = Voltage Regulator [part_number=LM317 package=to220-adj]
  Q2 = NPN-Transistor [part_number=S8050 package="TO92 [THT]"]
  R7 = Resistor [tolerance=±5% resistance=10 package=THT]

nets:
  N1: Part1.GND, R2.Pin_1, R3.Pin_1, Connector_+_GND.pin2, R6.leg1, J1.pin2
  N2: Part1.D2, S1.Pin_1, S1.Pin_2, R3.Pin_0
  N3: Part1.D3, J1.pin3
  N4: Part1.D4, J1.pin4
  N5: Part1.D5, J1.pin5
  N6: Part1.D6, J1.pin6
  N7: Part1.D7, J1.pin7
  N8: Part1.D8, Q2.B
  N9: Part1.D9, Q1.G, R4.Pin_0
  N10: Part1.VIN, Q1.S, R5.Pin_0
  N11: Part1.5V, S1.Pin_3, S1.Pin_4, R6.leg2, Q2.E
  N12: Part1.A2, Q1.D, Connector_+_GND.pin1, U2.IN
  N13: Part1.A1, R2.Pin_0, R5.Pin_1
  N14: Part1.A0, R6.wiper
  N15: Part1.3V3, J1.pin1
  N16: U2.ADJ, R7.Pin_0
  N17: U2.OUT, Q2.C
