# Fritzing sketch boxduino (saved by Fritzing 0.9.2b)
breadboards: 1

parts:
  Part1 = Arduino Nano (Rev3.0) (ICSP)
  R2 = Resistor [tolerance=±5% resistance=100k package=THT]
  S1 = Pushbutton [package="[THT]"]
  R3 = Resistor [tolerance=±5% resistance=1k package=THT]
  Q1 = MOSFET-NCHANNEL [part_number=3034 package=to220v]
  Connector_+_GND = female pin header, 2 pins [form="♀ (female)"]
  R4 = Resistor [tolerance=±5% resistance=1k package=THT]
  R5 = Resistor [tolerance=±5% resistance=1M package=THT]
  R6 = Rotary Potentiometer (Small) [maximum_resistance=50k package=THT]
  U1 = Voltage Regulator [package=to220-adj]
  R7 = Resistor [tolerance=±5% resistance=10 package=THT]
  Ohmmeter+ = female pin header, 1 pin [form="♀ (female)"]  # not connected
  J1 = PCD8544 LCD [form="♂ (male)" package=THT]

nets:
  N1: Part1.RESET, J1.DIN
  N2: Part1.GND, R2.Pin_1, R3.Pin_1, R6.leg1, J1.CE
  N3: Part1.D2, S1.Pin_1, S1.Pin_2, R3.Pin_0
  N4: Part1.D3, J1.GND
  N5: Part1.D4, J1.DC
  N6: Part1.D5, J1.CLK
  N7: Part1.D8, Q1.G, R4.Pin_0
  N8: Part1.D11/MOSI, J1.VCC
  N9: Part1.VIN, R5.Pin_0
  N10: Part1.5V, S1.Pin_3, S1.Pin_4, R6.leg2, U1.OUT
  N11: Part1.A2, U1.ADJ
  N12: Part1.A1, R2.Pin_0, R5.Pin_1
  N13: Part1.A0, R6.wiper
  N14: Part1.3V3, J1.RST
  N15: Part1.D13/SCK, J1.LIGHT
  N16: Q1.D, Connector_+_GND.pin2
  N17: Q1.S, Connector_+_GND.pin1
  N18: U1.IN, R7.Pin_0

custom parts:
  PCD8544 LCD: generic Nokia 5110 LCD
